# Fritzing sketch takeImg (saved by Fritzing 0.9.3b)
circuit board: 10.1895cm x 5.53631cm
breadboards: 1

parts:
  Esp32-cam1 = ESP32-Cam
  U1 = USB UART [package=ssop28db]

nets:
  5V: Esp32-cam1.5V, U1.VCC
  GND: Esp32-cam1.GND, U1.GND1
  N1: Esp32-cam1.GPIO_0, U1.GND2
  N2: Esp32-cam1.RX/GPIO_3, U1.TXD
  N3: Esp32-cam1.TX/GPIO_1, U1.RXD
